# Fritzing sketch Untitled Sketch2 (saved by Fritzing 0.9.3b)
breadboards: 1

parts:
  Componente1 = Arduino Nano (Rev3.0)
  LCD1 = LCD screen
  DS2 = DS18B20 1-Wire Temperature Sensor Probe Cable
  ENC28J1 = ENC28J60

nets:
  GND: Componente1.GND, LCD1.VSS, LCD1.V0, LCD1.R/W, LCD1.DB0, DS2.GND, ENC28J1.GND
  N1: Componente1.D2, LCD1.LED-
  N2: Componente1.D3, LCD1.LED+
  N3: Componente1.D4, LCD1.DB7
  N4: Componente1.D5, LCD1.DB6
  N5: Componente1.D6, Componente1.A3, DS2.shield
  N6: Componente1.D7, LCD1.E
  N7: Componente1.D8, LCD1.DB1
  N8: Componente1.D10, ENC28J1.CS
  N9: Componente1.D11/MOSI, ENC28J1.SI
  N10: Componente1.D12/MISO, ENC28J1.SO
  5V: Componente1.5V, LCD1.VDD, LCD1.RS, DS2.VDD, ENC28J1.5v
  N11: Componente1.D13/SCK, ENC28J1.SCK, ENC28J1.RST

custom parts:
  ENC28J60: Ethernet Module ENC28J60
